// Logisim project SevenSegDec.circ as structural Verilog: 1 circuit, main circuit SevenSegDec
module SevenSegDec (
  input  A3,
  input  A2,
  input  A1,
  input  A0,
  output S0,
  output S1,
  output S2,
  output S3,
  output S4,
  output S5,
  output S6
);

  wire and_1_out, and_2_out, and_3_out, and_4_out, and_5_out, and_6_out, and_7_out, and_8_out, and_9_out,
       and_10_out, and_11_out, and_12_out, and_13_out, and_14_out, and_15_out, and_16_out, and_17_out,
       and_18_out, and_19_out, and_20_out, and_21_out, and_22_out, and_23_out, and_24_out, and_25_out,
       and_26_out, and_27_out, and_28_out, and_29_out, and_30_out, and_31_out, and_32_out, and_33_out,
       and_34_out, and_35_out, and_36_out, not_1_out, not_2_out, not_3_out, not_4_out, not_5_out, not_6_out,
       not_7_out, not_8_out, not_9_out, not_10_out, not_11_out, or_1_out, or_2_out, or_3_out, or_4_out,
       or_5_out, or_6_out;

  not not_1 (not_1_out, A3);
  not not_2 (not_2_out, A2);
  not not_3 (not_3_out, A1);
  not not_4 (not_4_out, A0);
  not not_5 (not_5_out, not_2_out);
  and and_1 (and_1_out, not_1_out, not_2_out);
  and and_2 (and_2_out, not_1_out, A2);
  and and_3 (and_3_out, not_1_out, A2);
  and and_4 (and_4_out, not_1_out, A2);
  and and_5 (and_5_out, not_1_out, not_2_out);
  not not_6 (not_6_out, not_3_out);
  and and_6 (and_6_out, not_1_out, not_5_out);
  and and_7 (and_7_out, not_3_out, and_1_out);
  and and_8 (and_8_out, and_2_out, not_3_out);
  and and_9 (and_9_out, not_3_out, and_3_out);
  and and_10 (and_10_out, and_4_out, A1);
  not not_7 (not_7_out, not_1_out);
  and and_11 (and_11_out, and_5_out, not_6_out);
  and and_12 (and_12_out, and_6_out, not_3_out);
  and and_13 (and_13_out, not_4_out, and_7_out);
  and and_14 (and_14_out, not_4_out, and_8_out);
  and and_15 (and_15_out, and_9_out, A0);
  and and_16 (and_16_out, not_4_out, and_10_out);
  and and_17 (and_17_out, A0, and_11_out);
  and and_18 (and_18_out, A0, and_12_out);
  not not_8 (not_8_out, A0);
  or or_1 (or_1_out, and_13_out, and_14_out);
  or or_2 (or_2_out, and_15_out, and_16_out);
  or or_3 (or_3_out, and_17_out, and_18_out);
  and and_19 (and_19_out, not_1_out, A2);
  or or_4 (or_4_out, or_1_out, or_2_out);
  and and_20 (and_20_out, not_1_out, A2);
  not not_9 (not_9_out, A1);
  not not_10 (not_10_out, A2);
  and and_21 (and_21_out, not_10_out, not_1_out);
  and and_22 (and_22_out, not_2_out, not_7_out);
  and and_23 (and_23_out, not_1_out, not_2_out);
  and and_24 (and_24_out, A2, not_1_out);
  not not_11 (not_11_out, not_3_out);
  and and_25 (and_25_out, and_19_out, not_3_out);
  not not_12 (S1, or_4_out);
  and and_26 (and_26_out, not_11_out, and_20_out);
  and and_27 (and_27_out, not_9_out, and_21_out);
  and and_28 (and_28_out, not_3_out, and_22_out);
  and and_29 (and_29_out, and_28_out, not_8_out);
  and and_30 (and_30_out, A1, and_23_out);
  and and_31 (and_31_out, and_24_out, not_3_out);
  and and_32 (and_32_out, and_25_out, A0);
  and and_33 (and_33_out, A0, and_26_out);
  and and_34 (and_34_out, and_27_out, A0);
  and and_35 (and_35_out, and_30_out, not_4_out);
  and and_36 (and_36_out, A0, and_31_out);
  not not_13 (S2, and_32_out);
  nor nor_1 (S3, and_33_out, and_34_out);
  or or_5 (or_5_out, or_1_out, and_16_out);
  nor nor_2 (S4, and_29_out, or_3_out);
  or or_6 (or_6_out, and_35_out, and_36_out);
  not not_14 (S0, or_6_out);
  not not_15 (S6, or_5_out);
  _7_Segment_Display u_7_segment_display_1 (.g(S0), .f(S1), .a(S2), .b(S3), .e(S4), .d(S2), .c(S6));  // open: dp

  assign S5 = S2;

  // Notes on the sheet:
  //   Ye Yuan, 260921269
endmodule
